# Fritzing sketch Fotorezystor (saved by Fritzing 0.9.3b)
breadboards: 1

parts:
  Part1 = Arduino Uno (Rev3)
  LED1 = LED - 5mm [color="Red (635nm)" package="5 mm [THT]"]
  LED2 = LED - 5mm [color="Yellow (585nm)" package="5 mm [THT]"]
  LED3 = LED - 5mm [color="Green (560nm)" package="5 mm [THT]"]
  R1 = PHOTOCELL [package=photocell-kit]
  R2 = Resistor [tolerance=±5% resistance=220 package=THT]
  R3 = Resistor [tolerance=±5% resistance=220 package=THT]
  R4 = Resistor [tolerance=±5% resistance=220 package=THT]
  R5 = Resistor [tolerance=±5% resistance=10k package=THT]

nets:
  N1: Part1.A0, R1.P$2, R5.Pin_0
  N2: Part1.D9_PWM, R2.Pin_1
  N3: Part1.D10_PWM/SS, R3.Pin_1
  N4: Part1.D11_PWM/MOSI, R4.Pin_1
  N5: Part1.5V, R1.P$1
  N6: Part1.GND, LED1.cathode, LED2.cathode, LED3.cathode, R5.Pin_1
  N7: LED1.anode, R2.Pin_0
  N8: LED2.anode, R3.Pin_0
  N9: LED3.anode, R4.Pin_0

// code stored in the sketch: Fotorezystor.ino
enum led{
	red = 9,
  yellow = 10,
  green =11
};

const int photoPin = 0;
int val;
led diody;
double procenty;

void setup() {
  // put your setup code here, to run once:
  pinMode(photoPin,INPUT);
  pinMode(9,OUTPUT);
  pinMode(10,OUTPUT);
  pinMode(11,OUTPUT);
  Serial.begin(9600);
  diody = yellow;
}

void loop() {
  // put your main code here, to run repeatedly:
  val = analogRead(photoPin);
  procenty = val/1024.0*100.0;
  if(procenty < 33.0){
    digitalWrite(diody, LOW);
    diody = red;
  }
  else if(procenty >=33.0 && procenty < 66.0){
    digitalWrite(diody, LOW);
    diody = yellow;
  }
  else if(procenty>=66.0){
    digitalWrite(diody, LOW);
    diody = green;
  }
  digitalWrite(diody,HIGH);
  delay(1000);
}
