# Fritzing sketch Projekt od Michała (saved by Fritzing 0.9.3b)
breadboards: 1

parts:
  U1 = ESP-12F (ESP8266 WiFi Module) [part_number=ESP8266]
  U2 = Voltage Regulator - Variable [package="TO220 [THT]"]
  USBUART1 = PL2303 USB UART Breakout
  S1 = Pushbutton [package="[SMD]"]
  S2 = Pushbutton [package="[THT]"]
  R1 = Resistor [tolerance=±5% resistance=3.3k package=THT]
  R2 = Resistor [tolerance=±5% resistance=1.5k package="2512 [SMD]"]
  R3 = Resistor [tolerance=±5% resistance=100 package="2512 [SMD]"]

nets:
  N1: U1.RXD0, USBUART1.TXD
  N2: U1.VCC, U2.OUT, R1.Pin_0
  N3: U1.GPIO0, S1.Pin_1, S1.Pin_2
  N4: U1.GND, S1.Pin_3, S1.Pin_4, S2.Pin_3, S2.Pin_4, R3.Pin_1
  N5: U1.TXD0, USBUART1.RXD
  N6: U1.RST, S2.Pin_1, S2.Pin_2
  N7: U2.IN, R1.Pin_1, R2.Pin_0
  N8: R2.Pin_1, R3.Pin_0

custom parts:
  ESP-12F (ESP8266 WiFi Module): WiFi Module based on the ESP8266 with onboard PCB antenna and UART communications
  PL2303 USB UART Breakout: PL2302 Usb Uart Breakout Board with Battery
